# Fritzing sketch ir_sketch (saved by Fritzing 0.8.5b)
breadboards: 1

parts:
  LPD8806_RGB_LED_Strip1 = LPD8806 RGB LED Strip
  JACK1 = 2.1mm Barrel Jack with Terminal Block
  PIR1 = PIR sensor
  IC1 = MICROCONTROLLER [package=dil28-3-simon-kit]
  VCC1 = Battery

nets:
  GND: LPD8806_RGB_LED_Strip1.GND, JACK1.NEG, PIR1.GND, IC1.GND, VCC1.-
  N1: LPD8806_RGB_LED_Strip1.DI, IC1.PD0(RXD)
  N2: LPD8806_RGB_LED_Strip1.CI, IC1.PD1(TXD)
  N3: LPD8806_RGB_LED_Strip1.+5V, JACK1.POS
  N4: PIR1.VDD, VCC1.+
  N5: PIR1.SIG, IC1.PB0(ICP)
  N6: IC1.PC6(_RESET), IC1.PD6(AIN0)
  N7: IC1.PB7(XTAL2_TOSC2), IC1.PD5(T1)

custom parts:
  LPD8806 RGB LED Strip: Digitally addressable RGB LED strip
