# Fritzing sketch ir_schematic (saved by Fritzing 0.8.5b)

parts:
  PIR1 = PIR sensor
  LPD8806_RGB_LED_Strip1 = LPD8806 RGB LED Strip
  JACK1 = 2.1mm Barrel Jack with Terminal Block
  Part1 = Arduino Uno (Rev3)

nets:
  VDD: PIR1.VDD, Part1.5V
  N1: PIR1.SIG, Part1.D8
  GND: PIR1.GND, LPD8806_RGB_LED_Strip1.GND, JACK1.NEG, Part1.GND
  N2: LPD8806_RGB_LED_Strip1.DI, Part1.D3_PWM
  N3: LPD8806_RGB_LED_Strip1.CI, Part1.D2
  N4: LPD8806_RGB_LED_Strip1.+5V, JACK1.POS

custom parts:
  LPD8806 RGB LED Strip: Digitally addressable RGB LED strip
